# Fritzing sketch ActuatorControlPCB (saved by Fritzing 0.9.3b)
circuit board: 6.35cm x 5.08cm
breadboards: 1

parts:
  Nucleo_F031K6 = IC, DIP package, 30 pins [chip_label="Nucleo F031K6"]
  IdleSwitch = female pin header, 3 pins [form="♀ (female)"]
  ControlSwitch = female pin header, 3 pins [form="♀ (female)"]
  ActSwitch1 = female pin header, 3 pins [form="♀ (female)"]
  ActSwitch2 = female pin header, 3 pins [form="♀ (female)"]
  ActSwitch3 = female pin header, 3 pins [form="♀ (female)"]
  ActSwitch4 = female pin header, 3 pins [form="♀ (female)"]
  ExternalPower = female pin header, 3 pins [form="♀ (female)"]
  Header_Box = shrouded pin header, 16 pins [form="♂ (shrouded male)"]

nets:
  N1: Nucleo_F031K6.pin4, IdleSwitch.pin1, ControlSwitch.pin3, ActSwitch1.pin1, ActSwitch2.pin1, ActSwitch3.pin1, ActSwitch4.pin1
  N2: Nucleo_F031K6.pin6, ActSwitch1.pin2
  N3: Nucleo_F031K6.pin7, ActSwitch2.pin2
  N4: Nucleo_F031K6.pin8, ActSwitch3.pin2
  N5: Nucleo_F031K6.pin9, ActSwitch4.pin2
  N6: Nucleo_F031K6.pin10, ControlSwitch.pin2
  N7: Nucleo_F031K6.pin11, IdleSwitch.pin2
  N8: Nucleo_F031K6.pin12, Header_Box.pin10
  N9: Nucleo_F031K6.pin13, Header_Box.pin12
  N10: Nucleo_F031K6.pin14, Header_Box.pin14
  N11: Nucleo_F031K6.pin15, Header_Box.pin16
  N12: Nucleo_F031K6.pin17, IdleSwitch.pin3, ControlSwitch.pin1, ActSwitch1.pin3, ActSwitch2.pin3, ActSwitch3.pin3, ActSwitch4.pin3
  N13: Nucleo_F031K6.pin29, ExternalPower.pin2, ExternalPower.pin3, Header_Box.pin2, Header_Box.pin4, Header_Box.pin6, Header_Box.pin8, Header_Box.pin9, Header_Box.pin11, Header_Box.pin13, Header_Box.pin15
  N14: ExternalPower.pin1, Header_Box.pin1, Header_Box.pin3, Header_Box.pin5, Header_Box.pin7

notes:
  Whitworth University
  Linear Actuator Control Box
  Version 1          Jan 2020
  01/09/20
  Craig Russell
  (+)
  (-)
  Actuator Switches
  1
  2
  3
  4
  Idle
  Run
  Auto
  Manual
